# Fritzing sketch Feather32u4_Shift_In copy (saved by Fritzing 0.9.3b)
breadboards: 3

parts:
  Part1 = Adafruit Trinket M0 [part_number="Adafruit #3500"]
  IC1 = SHIFT REGISTER [part_number=74HC165 package=dil16]
  S1 = Momentary Switch [package=ksa_sealed_tac_switch]
  R2 = Resistor [tolerance=±5% resistance=220 package="1206 [SMD]"]
  R3 = Resistor [tolerance=±5% resistance=220 package="1206 [SMD]"]
  R4 = Resistor [tolerance=±5% resistance=220 package="1206 [SMD]"]
  S2 = Momentary Switch [package=ksa_sealed_tac_switch]
  S3 = Momentary Switch [package=ksa_sealed_tac_switch]
  R5 = Resistor [tolerance=±5% resistance=220 package="1206 [SMD]"]
  S4 = Momentary Switch [package=ksa_sealed_tac_switch]
  IC2 = SHIFT REGISTER [part_number=74HC165 package=dil16]  # not connected
  R7 = Resistor [tolerance=±5% resistance=220 package="1206 [SMD]"]
  S7 = Momentary Switch [package=ksa_sealed_tac_switch]
  S8 = Momentary Switch [package=ksa_sealed_tac_switch]
  R8 = Resistor [tolerance=±5% resistance=220 package="1206 [SMD]"]
  S9 = Momentary Switch [package=ksa_sealed_tac_switch]
  R9 = Resistor [tolerance=±5% resistance=220 package="1206 [SMD]"]
  S10 = Momentary Switch [package=ksa_sealed_tac_switch]
  R10 = Resistor [tolerance=±5% resistance=220 package="1206 [SMD]"]
  R11 = Resistor [tolerance=±5% resistance=220 package="1206 [SMD]"]
  R12 = Resistor [tolerance=±5% resistance=220 package="1206 [SMD]"]
  S11 = Momentary Switch [package=ksa_sealed_tac_switch]
  S12 = Momentary Switch [package=ksa_sealed_tac_switch]
  S13 = Momentary Switch [package=ksa_sealed_tac_switch]
  S14 = Momentary Switch [package=ksa_sealed_tac_switch]
  S15 = Momentary Switch [package=ksa_sealed_tac_switch]
  S16 = Momentary Switch [package=ksa_sealed_tac_switch]
  S17 = Momentary Switch [package=ksa_sealed_tac_switch]
  S18 = Momentary Switch [package=ksa_sealed_tac_switch]
  R13 = Resistor [tolerance=±5% resistance=220 package="1206 [SMD]"]
  R14 = Resistor [tolerance=±5% resistance=220 package="1206 [SMD]"]
  R15 = Resistor [tolerance=±5% resistance=220 package="1206 [SMD]"]
  R16 = Resistor [tolerance=±5% resistance=220 package="1206 [SMD]"]
  R17 = Resistor [tolerance=±5% resistance=220 package="1206 [SMD]"]
  R18 = Resistor [tolerance=±5% resistance=220 package="1206 [SMD]"]
  Part2 = Adafruit Feather 32u4 Basic Proto [part_number="Adafruit #2771"]  # not connected

nets:
  GND: Part1.GND, IC1.QH, IC1.GND, IC1.SCK, IC1.RCK, IC1.G, IC1.SER, R2.Pin_1, R3.Pin_1, R4.Pin_1, R5.Pin_1
  N1: Part1.D3_A3_PA07_RXD_SCK, IC1.QH*
  3.3V: Part1.3.3V, IC1.VCC, S1.1, S2.1, S3.1, S4.1
  N2: Part1.D2_A1_PA09_SCL_MISO, IC1.QB
  N3: Part1.D1_A0_PA02, IC1.QC
  N4: Part1.D0_A4_PA08_SDA, IC1.QA
  N5: IC1.QD, S1.4, R4.Pin_0
  N6: IC1.QE, R2.Pin_0, S2.4
  N7: IC1.QF, R3.Pin_0, S3.4
  N8: IC1.QG, R5.Pin_0, S4.4
  N9: R7.Pin_0, S7.4
  N10: R7.Pin_1, R8.Pin_1, R9.Pin_1, R10.Pin_1, R11.Pin_1, R12.Pin_1, R13.Pin_1, R14.Pin_1, R15.Pin_1, R16.Pin_1, R17.Pin_1, R18.Pin_1
  N11: S7.1, S8.1, S9.1, S10.1, S11.1, S12.1, S14.1, S15.1, S16.1, S17.1, S18.1
  N12: S8.4, R8.Pin_0
  N13: S9.4, R9.Pin_0
  N14: S10.4, R10.Pin_0
  N15: R11.Pin_0, S11.4
  N16: R12.Pin_0, S12.4
  N17: S13.4, R13.Pin_0
  N18: S14.4, R17.Pin_0
  N19: S15.4, R15.Pin_0
  N20: S16.4, R14.Pin_0
  N21: S17.4, R16.Pin_0
  N22: S18.4, R18.Pin_0

custom parts:
  Adafruit Feather 32u4 Basic Proto: At the Feather 32u4's heart is at ATmega32u4 clocked at 8 MHz and at 3.3V logic, a chip setup we've had tons of experience with as it's the same as the Flora. This chip has 32K of flash and 2K of RAM, with built in USB so not only does it have a USB-to-Serial program & debug capability built in with no need for an FTDI-like chip, it can also act like a mouse, keyboard, USB MIDI device, etc.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
