# Fritzing sketch TrinketM0_Shift_In (saved by Fritzing 0.9.3b)
breadboards: 1

parts:
  Part1 = Adafruit Trinket M0 [part_number="Adafruit #3500"]
  IC1 = SHIFT REGISTER [part_number=74HC165 package=dil16]
  S1 = Momentary Switch [package=ksa_sealed_tac_switch]
  R2 = Resistor [tolerance=±5% resistance=10k package="1206 [SMD]"]
  R3 = Resistor [tolerance=±5% resistance=10k package="1206 [SMD]"]
  R4 = Resistor [tolerance=±5% resistance=10k package="1206 [SMD]"]
  S2 = Momentary Switch [package=ksa_sealed_tac_switch]
  S3 = Momentary Switch [package=ksa_sealed_tac_switch]
  R5 = Resistor [tolerance=±5% resistance=10k package="1206 [SMD]"]
  S4 = Momentary Switch [package=ksa_sealed_tac_switch]

nets:
  GND: Part1.GND, IC1.QH, IC1.GND, IC1.SCK, IC1.RCK, IC1.G, IC1.SER, R2.Pin_1, R3.Pin_1, R4.Pin_1, R5.Pin_1
  N1: Part1.D3_A3_PA07_RXD_SCK, IC1.QH*
  3.3V: Part1.3.3V, IC1.VCC, S1.1, S2.1, S3.1, S4.1
  N2: Part1.D2_A1_PA09_SCL_MISO, IC1.QB
  N3: Part1.D1_A0_PA02, IC1.QC
  N4: Part1.D0_A4_PA08_SDA, IC1.QA
  N5: IC1.QD, S1.4, R4.Pin_0
  N6: IC1.QE, R2.Pin_0, S2.4
  N7: IC1.QF, R3.Pin_0, S3.4
  N8: IC1.QG, R5.Pin_0, S4.4
