# Fritzing sketch feather_shift_in_single (saved by Fritzing 1.0.6)
breadboards: 1

parts:
  Part3 = Adafruit Feather 32u4 Basic Proto [part_number="Adafruit #2771"]
  R24 = Resistor [tolerance=±5% resistance=10k package="1206 [SMD]"]
  R26 = Resistor [tolerance=±5% resistance=10k package="1206 [SMD]"]
  R29 = Resistor [tolerance=±5% resistance=10k package="1206 [SMD]"]
  S19 = Momentary Switch [package=ksa_sealed_tac_switch]
  S20 = Momentary Switch [package=ksa_sealed_tac_switch]
  S21 = Momentary Switch [package=ksa_sealed_tac_switch]
  S22 = Momentary Switch [package=ksa_sealed_tac_switch]
  S23 = Momentary Switch [package=ksa_sealed_tac_switch]
  S24 = Momentary Switch [package=ksa_sealed_tac_switch]
  S25 = Momentary Switch [package=ksa_sealed_tac_switch]
  S26 = Momentary Switch [package=ksa_sealed_tac_switch]
  IC4 = 74HC165 [part_number=74HC165 package=dil16]
  R30 = Resistor [tolerance=±5% resistance=10k package="1206 [SMD]"]
  R31 = Resistor [tolerance=±5% resistance=10k package="1206 [SMD]"]
  R32 = Resistor [tolerance=±5% resistance=10k package="1206 [SMD]"]
  R33 = Resistor [tolerance=±5% resistance=10k package="1206 [SMD]"]
  R34 = Resistor [tolerance=±5% resistance=10k package="1206 [SMD]"]

nets:
  N1: Part3.GND, Part3.11
  N2: Part3.1, Part3.VBAT
  N3: Part3.0, Part3.A0, R24.Pin_0, R26.Pin_0, R29.Pin_0, IC4.QH, IC4.GND, R30.Pin_0, R31.Pin_0, R32.Pin_0, R33.Pin_0, R34.Pin_0
  N4: Part3.MISO, Part3.A1, IC4.QB
  N5: Part3.MOSI, S25.1
  N6: Part3.SCK, Part3.AREF, Part3.RST, Part3.12, Part3.2, S19.2, S20.2, S21.2, S22.2, S23.2, S24.2, S25.2, S26.2, IC4.VCC
  N7: Part3.A5, Part3.9
  N8: Part3.A4, S22.1
  N9: Part3.13, S22.4
  N10: Part3.5, S26.4, IC4.QG
  N11: R24.Pin_1, S25.3
  N12: R26.Pin_1, S26.3
  N13: R29.Pin_1, S23.3, IC4.SER
  N14: S19.3, IC4.SCK, R32.Pin_1
  N15: S20.3, R31.Pin_1
  N16: S20.4, IC4.QD
  N17: S21.3, IC4.G, R34.Pin_1
  N18: S22.3, IC4.RCK, R33.Pin_1
  N19: S24.3, R30.Pin_1
  N20: S24.4, IC4.QE
  N21: S25.4, IC4.QF

custom parts:
  Adafruit Feather 32u4 Basic Proto: At the Feather 32u4's heart is at ATmega32u4 clocked at 8 MHz and at 3.3V logic, a chip setup we've had tons of experience with as it's the same as the Flora. This chip has 32K of flash and 2K of RAM, with built in USB so not only does it have a USB-to-Serial program & debug capability built in with no need for an FTDI-like chip, it can also act like a mouse, keyboard, USB MIDI device, etc.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
  74HC165: 8-bit SHIFT REGISTER, output latch
