# Fritzing sketch Feather32u4_Shift_Out (saved by Fritzing 0.9.3b)
breadboards: 2

parts:
  IC1 = SHIFT REGISTER [part_number=74HC595 package=dil16]
  Part2 = Adafruit Feather 32u4 Basic Proto [part_number="Adafruit #2771"]
  R6 = Resistor [tolerance=±5% resistance=15 package=THT]
  R7 = Resistor [tolerance=±5% resistance=15 package=THT]
  LED2 = LED - 5mm [color="Red (633nm)" package="5 mm [THT]"]
  R8 = Resistor [tolerance=±5% resistance=15 package=THT]
  LED3 = LED - 5mm [color="Red (633nm)" package="5 mm [THT]"]
  R9 = Resistor [tolerance=±5% resistance=15 package=THT]
  LED4 = LED - 5mm [color="Red (633nm)" package="5 mm [THT]"]
  R10 = Resistor [tolerance=±5% resistance=15 package=THT]
  LED5 = LED - 5mm [color="Red (633nm)" package="5 mm [THT]"]
  R11 = Resistor [tolerance=±5% resistance=15 package=THT]
  LED6 = LED - 5mm [color="Red (633nm)" package="5 mm [THT]"]
  R12 = Resistor [tolerance=±5% resistance=15 package=THT]
  LED7 = LED - 5mm [color="Red (633nm)" package="5 mm [THT]"]
  R13 = Resistor [tolerance=±5% resistance=15 package=THT]
  LED8 = LED - 5mm [color="Red (633nm)" package="5 mm [THT]"]
  LED9 = LED - 5mm [color="Red (633nm)" package="5 mm [THT]"]

nets:
  N1: IC1.QB, LED7.anode
  N2: IC1.QC, LED6.anode
  N3: IC1.QD, LED5.anode
  N4: IC1.QE, LED4.anode
  N5: IC1.QF, LED3.anode
  N6: IC1.QG, LED2.anode
  N7: IC1.QH, LED9.anode
  GND: IC1.GND, IC1.G, Part2.GND, R6.Pin_0, R7.Pin_0, R8.Pin_0, R9.Pin_0, R10.Pin_0, R11.Pin_0, R12.Pin_0, R13.Pin_0
  VCC: IC1.SCL, IC1.VCC, Part2.+3V3
  N8: IC1.SCK, Part2.6
  N9: IC1.RCK, Part2.5
  N10: IC1.SER, Part2.9
  N11: IC1.QA, LED8.anode
  N12: R6.Pin_1, LED9.cathode
  N13: R7.Pin_1, LED2.cathode
  N14: R8.Pin_1, LED3.cathode
  N15: R9.Pin_1, LED4.cathode
  N16: R10.Pin_1, LED5.cathode
  N17: R11.Pin_1, LED6.cathode
  N18: R12.Pin_1, LED7.cathode
  N19: R13.Pin_1, LED8.cathode

custom parts:
  Adafruit Feather 32u4 Basic Proto: At the Feather 32u4's heart is at ATmega32u4 clocked at 8 MHz and at 3.3V logic, a chip setup we've had tons of experience with as it's the same as the Flora. This chip has 32K of flash and 2K of RAM, with built in USB so not only does it have a USB-to-Serial program & debug capability built in with no need for an FTDI-like chip, it can also act like a mouse, keyboard, USB MIDI device, etc.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
