# Fritzing sketch DRV8833 DC Motor (saved by Fritzing 0.9.3b)
breadboards: 1

parts:
  Part1 = Adafruit DRV8833 DC/Stepper Motor Driver [part_number="Adafruit #3297"]
  Part2 = Adafruit Feather M0 Basic Proto [part_number="Adafruit #2772"]
  M1 = DC Motor

nets:
  GND: Part1.GND, Part2.GND
  N1: Part1.AOUT2, M1.pin_1
  N2: Part1.AOUT1, M1.pin_2
  N3: Part1.VMOTOR, Part2.VBUS
  N4: Part1.!SLEEP, Part2.+3V3
  N5: Part1.AIN2, Part2.D11
  N6: Part1.AIN1, Part2.D10

custom parts:
  Adafruit DRV8833 DC/Stepper Motor Driver: Spin two DC motors or step one bi-polar or uni-polar stepper with up to 1.2A per channel using the DRV8833. This motor driver chip is a nice alternative to the TB6612 driver. Like that chip, you get 2 full H-bridges, but this chip is better for low voltage uses (can run from 2.7V up to 10.8V motor power) and has built in current limiting capability. We set it up for 1A current limiting so you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
  Adafruit Feather M0 Basic Proto: At the Feather M0's heart is an ATSAMD21G18 ARM Cortex M0 processor, clocked at 48 MHz and at 3.3V logic, the same one used in the new Arduino Zero. This chip has a whopping 256K of FLASH (8x more than the Atmega328 or 32u4) and 32K of RAM (16x as much)! This chip comes with built in USB so it has USB-to-Serial program & debug capability built in with no need for an FTDI-like chip. To make it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
