# Fritzing sketch DRV8880 (saved by Fritzing 0.9.3b)
breadboards: 1

parts:
  Part2 = Adafruit Feather 32u4 Basic Proto [part_number="Adafruit #2771"]
  VCC1 = Battery block 9V
  M1 = Stepper Motor - Bipolar
  Pololu_A1 = Pololu A4988 [package=SO16]
  C1 = Electrolytic Capacitor [capacitance=100µF package="100 mil [THT, electrolytic]"]

nets:
  N1: Part2.GND, VCC1.-, Pololu_A1.STEP, C1.-
  N2: Part2.+3V3, Pololu_A1.2B
  N3: Part2.6, Pololu_A1.GND#14
  N4: Part2.5, Pololu_A1.VMOT
  N5: VCC1.+, Pololu_A1.DIR, C1.+
  N6: M1.A, Pololu_A1.SLEEP
  N7: M1.C, Pololu_A1.RESET
  N8: M1.B, Pololu_A1.MS3
  N9: M1.D, Pololu_A1.MS2

custom parts:
  Adafruit Feather 32u4 Basic Proto: At the Feather 32u4's heart is at ATmega32u4 clocked at 8 MHz and at 3.3V logic, a chip setup we've had tons of experience with as it's the same as the Flora. This chip has 32K of flash and 2K of RAM, with built in USB so not only does it have a USB-to-Serial program & debug capability built in with no need for an FTDI-like chip, it can also act like a mouse, keyboard, USB MIDI device, etc.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
