# Fritzing sketch HC-SR04 (saved by Fritzing 0.9.3b)
breadboards: 1

parts:
  Part1 = Adafruit Feather 32u4 Basic Proto [part_number="Adafruit #2771"]
  hc-sr1 = hc-sr04

nets:
  GND: Part1.GND, hc-sr1.GND
  N1: Part1.VBUS, hc-sr1.VCC
  N2: Part1.6, hc-sr1.Trig
  N3: Part1.5, hc-sr1.Echo

custom parts:
  Adafruit Feather 32u4 Basic Proto: At the Feather 32u4's heart is at ATmega32u4 clocked at 8 MHz and at 3.3V logic, a chip setup we've had tons of experience with as it's the same as the Flora. This chip has 32K of flash and 2K of RAM, with built in USB so not only does it have a USB-to-Serial program & debug capability built in with no need for an FTDI-like chip, it can also act like a mouse, keyboard, USB MIDI device, etc.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
